# Fritzing sketch Sub_Osc_Comparetor (saved by Fritzing 0.9.4)
breadboards: 1

parts:
  IC1 = Dual Op-Amp [package=dip08]
  R1 = Resistor [tolerance=±5% resistance=10k package=THT]
  R2 = Resistor [tolerance=±5% resistance=1k package=THT]
  R3 = Resistor [tolerance=±5% resistance=1.8k package=THT]
  C1 = Electrolytic Capacitor [capacitance=1µF package="100 mil [THT, electrolytic]"]
  R6 = Resistor [tolerance=±5% resistance=10k package=THT]
  D1 = Rectifier Diode [part_number=1N4001 package="300 mil [THT]"]
  C2 = Ceramic Capacitor [capacitance=100nF package="100 mil [THT, multilayer]"]
  C3 = Ceramic Capacitor [capacitance=100nF package="100 mil [THT, multilayer]"]
  C4 = Electrolytic Capacitor [capacitance=1µF package="100 mil [THT, electrolytic]"]
  C5 = Electrolytic Capacitor [capacitance=1µF package="100 mil [THT, electrolytic]"]
  IC2 = IC, DIP package, 14 pins [chip_label=CD4013]
  C6 = Ceramic Capacitor [capacitance=100nF package="100 mil [THT, multilayer]"]

nets:
  N1: IC1.A_OUT, R6.Pin_1
  N2: IC1.A_-IN, R1.Pin_0, D1.anode, C2.1, C3.1, C4.+, C5.-, IC2.pin4, IC2.pin6, IC2.pin7, IC2.pin8, IC2.pin10, C6.0
  N3: IC1.A_V-, C2.0, C4.-
  N4: IC1.B_+IN, R1.Pin_1, R3.Pin_0
  N5: IC1.B_-IN, IC1.B_OUT, R2.Pin_1
  N6: IC1.A_V+, C3.0, C5.+, IC2.pin14, C6.1
  N7: R3.Pin_1, C1.-
  N8: R6.Pin_0, D1.cathode
  N9: IC2.pin1, IC2.pin11
  N10: IC2.pin2, IC2.pin5
  N11: IC2.pin9, IC2.pin12

notes:
  Out Stage
  Input
  +12V SQR
  Out Stage
  Output
  In Stage
  Output
  In Stage
  Input
  +/-5V SQR
  GND
  +12V
  -12V
  GND
  CD4013
  1 Q1 14 VDD
  2 !Q1 13 Q2
  3 CLK1 12 !Q2
  4 RES1 11 CLK2
  5 D1 10 RES2
  6 SET1 9 D2
  7 VSS 8 SET2
  1/4
  1/2
  IN
