# Fritzing sketch Sub_Osc_Comparetor2 (saved by Fritzing 0.9.4)
breadboards: 1

parts:
  IC1 = Dual Op-Amp [package=dip08]
  R1 = Resistor [tolerance=±5% resistance=10k package=THT]
  R2 = Resistor [tolerance=±5% resistance=1k package=THT]
  R3 = Resistor [tolerance=±5% resistance=1.8k package=THT]
  C1 = Electrolytic Capacitor [capacitance=1µF package="100 mil [THT, electrolytic]"]
  R6 = Resistor [tolerance=±5% resistance=1k package=THT]
  D1 = Rectifier Diode [part_number=1N4001 package="300 mil [THT]"]
  C2 = Ceramic Capacitor [capacitance=100nF package="100 mil [THT, multilayer]"]
  C3 = Ceramic Capacitor [capacitance=100nF package="100 mil [THT, multilayer]"]
  C4 = Electrolytic Capacitor [capacitance=1µF package="100 mil [THT, electrolytic]"]
  C5 = Electrolytic Capacitor [capacitance=1µF package="100 mil [THT, electrolytic]"]
  IC2 = IC, DIP package, 14 pins [chip_label=CD4013]
  C6 = Ceramic Capacitor [capacitance=100nF package="100 mil [THT, multilayer]"]
  IC3 = Dual Op-Amp [package=dip08]
  C7 = Ceramic Capacitor [capacitance=100nF package="100 mil [THT, multilayer]"]
  C8 = Ceramic Capacitor [capacitance=100nF package="100 mil [THT, multilayer]"]
  R7 = Resistor [tolerance=±5% resistance=1.8k package=THT]
  R8 = Resistor [tolerance=±5% resistance=10k package=THT]
  R9 = Resistor [tolerance=±5% resistance=1k package=THT]
  C9 = Electrolytic Capacitor [capacitance=1µF package="100 mil [THT, electrolytic]"]

nets:
  N1: IC1.A_OUT, IC1.A_-IN, R9.Pin_1
  N2: IC1.A_+IN, R7.Pin_0, R8.Pin_0
  N3: IC1.A_V-, C2.0, C4.-, IC3.A_V-, C7.0
  N4: IC1.B_+IN, R1.Pin_1, R3.Pin_0
  N5: IC1.B_-IN, IC1.B_OUT, R2.Pin_1
  N6: IC1.A_V+, C3.0, C5.+, IC2.pin14, C6.0, IC3.A_V+, C8.0
  N7: R1.Pin_0, D1.anode, C2.1, C3.1, C4.+, C5.-, IC2.pin4, IC2.pin6, IC2.pin7, IC2.pin8, IC2.pin10, C6.1, IC3.A_-IN, IC3.A_+IN, IC3.B_+IN, C7.1, C8.1, R8.Pin_1
  N8: R3.Pin_1, C1.-
  N9: C1.+, IC2.pin13
  N10: R6.Pin_0, D1.cathode, IC2.pin3
  N11: R6.Pin_1, IC3.A_OUT
  N12: IC2.pin1, IC2.pin11, C9.+
  N13: IC2.pin2, IC2.pin5
  N14: IC2.pin9, IC2.pin12
  N15: IC3.B_-IN, IC3.B_OUT
  N16: R7.Pin_1, C9.-

notes:
  1/4 OUT
  GND
  +12V
  -12V
  GND
  CD4013
  1 Q1 14 VDD
  2 !Q1 13 Q2
  3 CLK1 12 !Q2
  4 RES1 11 CLK2
  5 D1 10 RES2
  6 SET1 9 D2
  7 VSS 8 SET2
  1/2
  OUT
  IN
